# Fritzing sketch relay_button_connection (saved by Fritzing 0.9.8b)
breadboards: 1

parts:
  Teensy_LC1 = Teensy-LC
  8_Channel_Relay1 = 8 Channel Power Relay
  S1 = Pushbutton [package="[SMD]"]
  S2 = Pushbutton [package="[SMD]"]
  VALVE1 = Plastic Solenoid Valve
  Power_plug1 = Power plug
  VALVE2 = Plastic Solenoid Valve

nets:
  GND: Teensy_LC1.GND, 8_Channel_Relay1.GND
  N1: Teensy_LC1.D12, Teensy_LC1.5Vout
  N2: Teensy_LC1.Program, Teensy_LC1.A12/DAC, Teensy_LC1.D13, S2.Pin_1, S2.Pin_2
  N3: Teensy_LC1.A0/D14, 8_Channel_Relay1.IN2
  N4: Teensy_LC1.A1/D15, S1.Pin_1, S1.Pin_2
  N5: Teensy_LC1.A2/D16, 8_Channel_Relay1.IN1
  N6: Teensy_LC1.A7/D21, Teensy_LC1.A11
  N7: Teensy_LC1.A8/D22, Teensy_LC1.A10
  N8: Teensy_LC1.A9/D23, Teensy_LC1.AREF
  N9: Teensy_LC1.3V3, S1.Pin_3, S1.Pin_4, S2.Pin_3, S2.Pin_4
  N10: Teensy_LC1.AGND, Teensy_LC1.VUSB
  VIN: Teensy_LC1.Vin, 8_Channel_Relay1.VCC
  N11: 8_Channel_Relay1.NC#21, VALVE1.no_name_yet#1
  N12: 8_Channel_Relay1.COM#22, Power_plug1.VCC
  N13: 8_Channel_Relay1.NO, 8_Channel_Relay1.COM#25
  N14: 8_Channel_Relay1.NC#24, VALVE2.no_name_yet#1
  N15: VALVE1.no_name_yet#2, Power_plug1.GND, VALVE2.no_name_yet#2

notes:
  NC - COMMON - NO
  In NC:
  - HIGH Signal = current flows
  - LOW Signal = no flow
  In NO:
  - HIGH Signal = no flow
  - LOW Signal = current flows
  ! Relay ist beim Einschalten immer zu

custom parts:
  Teensy-LC: Teensy-LC (Low Cost) is a powerful 32 bit microcontroller board, with a rich set of hardware peripherals, at a very affordable price! Teensy-LC delivers an impressive collection of capabilities to make modern electronic projects simpler. It features an ARM Cortex-M0+ processor at 48 MHz, 62K Flash, 8K RAM, 12 bit analog input & output, hardware Serial, SPI & I2C, USB, and a total of 27 I/O pins.
  8 Channel Power Relay: An 8 channel power relay. The module operates at 5V.
